// Logisim project proiect.circ as structural Verilog
module main (
  input  in_1,
  input  [7:0] in_2
);

  wire button_1_out, button_2_out, button_3_out, sistem_1_p6, sistem_1_p7, sistem_1_p9, sistem_1_p12,
       sistem_1_p13, sistem_1_p14, sistem_1_p15, sistem_1_p16, sistem_1_p17;
  wire [6:0] sistem_1_p8, sistem_1_p10, sistem_1_p11;

  Button button_1 (.out(button_1_out));
  Button button_2 (.out(button_2_out));
  Button button_3 (.out(button_3_out));
  // sistem sistem_1: pin names not known; wires that end beside it: button_1_out, button_2_out, button_3_out, in_1, in_2, sistem_1_p6, sistem_1_p7, sistem_1_p8, sistem_1_p9, sistem_1_p10, sistem_1_p11, sistem_1_p12, sistem_1_p13, sistem_1_p14, sistem_1_p15, sistem_1_p16, sistem_1_p17
  _7_Segment_Display u_7_segment_display_1 (
    .g(sistem_1_p11[6]), .f(sistem_1_p11[5]), .a(sistem_1_p11[0]), .b(sistem_1_p11[1]), .e(sistem_1_p11[4]),
    .d(sistem_1_p11[3]), .c(sistem_1_p11[2]));  // open: dp
  LED led_1 (.in(sistem_1_p6));
  LED led_2 (.in(sistem_1_p7));
  LED led_3 (.in(sistem_1_p9));
  LED led_4 (.in(sistem_1_p12));
  LED led_5 (.in(sistem_1_p13));
  LED led_6 (.in(sistem_1_p14));
  LED led_7 (.in(sistem_1_p15));
  LED led_8 (.in(sistem_1_p16));
  LED led_9 (.in(sistem_1_p17));
  _7_Segment_Display u_7_segment_display_2 (
    .g(sistem_1_p10[6]), .f(sistem_1_p10[5]), .a(sistem_1_p10[0]), .b(sistem_1_p10[1]), .e(sistem_1_p10[4]),
    .d(sistem_1_p10[3]), .c(sistem_1_p10[2]));  // open: dp
  _7_Segment_Display u_7_segment_display_3 (
    .g(sistem_1_p8[6]), .f(sistem_1_p8[5]), .a(sistem_1_p8[0]), .b(sistem_1_p8[1]), .e(sistem_1_p8[4]),
    .d(sistem_1_p8[3]), .c(sistem_1_p8[2]));  // open: dp
endmodule

module decodificator (
  input  [7:0] Bin_num,
  output [6:0] Unitati,
  output [6:0] Zeci,
  output [6:0] Sute
);

  wire n7447_1_pin3;
  wire [3:0] binary_to_decimal_converter_1_decimal, binary_to_decimal_converter_1_hundred,
       binary_to_decimal_converter_1_unit;
  wire [6:0] n7447_1_pin13, n7447_2_pin13, n7447_3_pin13;

  Binary_to_decimal_converter binary_to_decimal_converter_1 (
    .Bin_num(Bin_num), .Unit(binary_to_decimal_converter_1_unit),
    .Decimal(binary_to_decimal_converter_1_decimal), .Hundred(binary_to_decimal_converter_1_hundred));
  _7447 #(.ShowInternalStructure("true")) u_7447_1 (
    .pin1(binary_to_decimal_converter_1_unit[1]), .pin2(binary_to_decimal_converter_1_unit[2]),
    .pin3(n7447_1_pin3), .pin4(n7447_1_pin3), .pin5(n7447_1_pin3),
    .pin6(binary_to_decimal_converter_1_unit[3]), .pin7(binary_to_decimal_converter_1_unit[0]),
    .pin15(n7447_1_pin13[5]), .pin14(n7447_1_pin13[6]), .pin13(n7447_1_pin13[0]), .pin12(n7447_1_pin13[1]),
    .pin11(n7447_1_pin13[2]), .pin10(n7447_1_pin13[3]), .pin9(n7447_1_pin13[4]));
  _7447 #(.ShowInternalStructure("true")) u_7447_2 (
    .pin1(binary_to_decimal_converter_1_decimal[1]), .pin2(binary_to_decimal_converter_1_decimal[2]),
    .pin3(n7447_1_pin3), .pin4(n7447_1_pin3), .pin5(n7447_1_pin3),
    .pin6(binary_to_decimal_converter_1_decimal[3]), .pin7(binary_to_decimal_converter_1_decimal[0]),
    .pin15(n7447_2_pin13[5]), .pin14(n7447_2_pin13[6]), .pin13(n7447_2_pin13[0]), .pin12(n7447_2_pin13[1]),
    .pin11(n7447_2_pin13[2]), .pin10(n7447_2_pin13[3]), .pin9(n7447_2_pin13[4]));
  _7447 u_7447_3 (
    .pin1(binary_to_decimal_converter_1_hundred[1]), .pin2(binary_to_decimal_converter_1_hundred[2]),
    .pin3(n7447_1_pin3), .pin4(n7447_1_pin3), .pin5(n7447_1_pin3),
    .pin6(binary_to_decimal_converter_1_hundred[3]), .pin7(binary_to_decimal_converter_1_hundred[0]),
    .pin15(n7447_3_pin13[5]), .pin14(n7447_3_pin13[6]), .pin13(n7447_3_pin13[0]), .pin12(n7447_3_pin13[1]),
    .pin11(n7447_3_pin13[2]), .pin10(n7447_3_pin13[3]), .pin9(n7447_3_pin13[4]));
  assign Zeci = ~n7447_2_pin13;  // NOT_Gate not_1, 7 bits wide
  assign Sute = ~n7447_3_pin13;  // NOT_Gate not_2, 7 bits wide
  assign Unitati = ~n7447_1_pin13;  // NOT_Gate not_3, 7 bits wide
  // also tied to VCC on the sheet: n7447_1_pin3
endmodule

module sistem (
  input  start,
  input  OK,
  input  RESET,
  input  DEBUG,
  input  [7:0] SWITCH,
  output FINAL,
  output REST,
  output BANI,
  output LEGITIMATIE,
  output CLASA,
  output KM,
  output WAITING,
  output [6:0] UNITATI,
  output [6:0] ZECI,
  output [6:0] SUTE,
  output REST_IMP,
  output Bancnote_final
);

  wire and_1_out, and_2_out, and_3_out, and_4_out, and_5_out, and_7_out, and_8_out, and_9_out, and_10_out,
       CLK, insert_coin_1_zero, j_k_ff_1_q, j_k_ff_2_q, j_k_ff_3_q, multiplexer_7_out, multiplexer_8_out,
       n7442_1_pin1, n7442_1_pin2, n7442_1_pin3, n7442_1_pin4, n7442_1_pin5, n7442_1_pin6, n7442_2_pin2,
       n7442_2_pin3, n7442_2_pin4, n7442_2_pin5, n7442_2_pin6, n7442_2_pin12, not_1_out, not_2_out,
       not_3_out, not_4_out, not_5_out, not_6_out, or_1_out, or_2_out, or_3_out, or_4_out, or_5_out,
       or_6_out, or_7_out, or_8_out, or_9_out, REST_t, uc_1_waiting;
  wire [2:0] MODE;
  wire [7:0] AR, EURO1, EURO2, EURO5, EURO10, EURO20, EURO50, MEMORIE_KM, multiplexer_1_out,
       multiplexer_2_out, multiplexer_3_out, multiplexer_4_out, multiplexer_5_out, multiplexer_6_out,
       multiplexer_9_out, multiplexer_10_out, PRET, QEURO1, QEURO2, QEURO5, QEURO10, QEURO20, QEURO50,
       SUMA_IN, SUMA_OUT;
  wire [7:2] counter_1_q;

  Clock clock_1 (.out(CLK));
  Multiplexer #(.width(8)) multiplexer_1 (.in0(SWITCH), .in1(QEURO1), .out(multiplexer_1_out), .sel(FINAL));
  Multiplexer #(.width(8)) multiplexer_2 (.in0(SWITCH), .in1(QEURO2), .out(multiplexer_2_out), .sel(FINAL));
  Multiplexer #(.width(8)) multiplexer_3 (.in0(SWITCH), .in1(QEURO5), .out(multiplexer_3_out), .sel(FINAL));
  Multiplexer #(.width(8)) multiplexer_4 (.in0(SWITCH), .in1(QEURO10), .out(multiplexer_4_out), .sel(FINAL));
  Multiplexer #(.width(8)) multiplexer_5 (.in0(SWITCH), .in1(QEURO20), .out(multiplexer_5_out), .sel(FINAL));
  Multiplexer #(.width(8)) multiplexer_6 (.in0(SWITCH), .in1(QEURO50), .out(multiplexer_6_out), .sel(FINAL));
  and and_1 (and_1_out, OK, DEBUG);
  Counter #(.max('h6)) counter_1 (
    .clr(start), .load(1'b0), .up(1'b1), .clk(and_1_out), .carry(Bancnote_final),
    .Q({counter_1_q[7:5], counter_1_q[5], counter_1_q[3:2], {2{counter_1_q[5]}}}));  // open: count, D
  _7442 #(.ShowInternalStructure("true")) u_7442_1 (
    .pin1(n7442_1_pin1), .pin2(n7442_1_pin2), .pin3(n7442_1_pin3), .pin4(n7442_1_pin4), .pin5(n7442_1_pin5),
    .pin6(n7442_1_pin6), .pin15(counter_1_q[5]), .pin14(counter_1_q[5]), .pin13(counter_1_q[5]),
    .pin12(counter_1_q[5]));  // open: pin7, pin11, pin10, pin9
  and and_2 (and_2_out, DEBUG, not_1_out);
  or or_1 (or_1_out, FINAL, and_2_out);
  not not_1 (not_1_out, n7442_1_pin1);
  not not_2 (not_2_out, n7442_1_pin2);
  not not_3 (not_3_out, n7442_1_pin3);
  not not_4 (not_4_out, n7442_1_pin4);
  and and_3 (and_3_out, DEBUG, not_2_out);
  and and_4 (and_4_out, DEBUG, not_3_out);
  and and_5 (and_5_out, DEBUG, not_4_out);
  or or_2 (or_2_out, FINAL, and_3_out);
  or or_3 (or_3_out, FINAL, and_4_out);
  or or_4 (or_4_out, FINAL, and_5_out);
  UC uc_1 (
    .START(start), .OK(OK), .CLK(CLK), .RESET(RESET), .INSERT_MONEY(REST_t), .DEBUG(DEBUG), .MODE(MODE),
    .Waiting(uc_1_waiting), .FINALE(FINAL));
  and and_6 (WAITING, uc_1_waiting, CLK);
  Mem_Reg MEMORIE_1EURO (.Clk(CLK), .Ld(or_1_out), .Rst(RESET), .Data(multiplexer_1_out), .Q(EURO1));
  Mem_Reg MEMORIE_2EURO (.Clk(CLK), .Ld(or_2_out), .Rst(RESET), .Data(multiplexer_2_out), .Q(EURO2));
  Mem_Reg MEMORIE_5EURO (.Clk(CLK), .Ld(or_3_out), .Rst(RESET), .Data(multiplexer_3_out), .Q(EURO5));
  Mem_Reg MEMORIE_10EURO (.Clk(CLK), .Ld(or_4_out), .Rst(RESET), .Data(multiplexer_4_out), .Q(EURO10));
  Mem_Reg MEMORIE_20EURO (.Clk(CLK), .Ld(or_5_out), .Rst(RESET), .Data(multiplexer_5_out), .Q(EURO20));
  Mem_Reg MEMORIE_50EURO (.Clk(CLK), .Ld(or_6_out), .Rst(RESET), .Data(multiplexer_6_out), .Q(EURO50));
  not not_5 (not_5_out, n7442_1_pin5);
  not not_6 (not_6_out, n7442_1_pin6);
  and and_7 (and_7_out, DEBUG, not_5_out);
  and and_8 (and_8_out, DEBUG, not_6_out);
  or or_5 (or_5_out, FINAL, and_7_out);
  or or_6 (or_6_out, FINAL, and_8_out);
  Mem_Reg MEMORIE_KILOMETRI (.Clk(CLK), .Ld(KM), .Rst(RESET), .Data(SWITCH), .Q(MEMORIE_KM));
  _7442 #(.ShowInternalStructure("true")) u_7442_2 (
    .pin2(n7442_2_pin2), .pin3(n7442_2_pin3), .pin4(n7442_2_pin4), .pin5(n7442_2_pin5), .pin6(n7442_2_pin6),
    .pin15(MODE[0]), .pin14(MODE[1]), .pin13(MODE[2]), .pin12(n7442_2_pin12));  // open: pin1, pin7, pin11, pin10, pin9
  not not_7 (KM, n7442_2_pin2);
  not not_8 (CLASA, n7442_2_pin3);
  not not_9 (LEGITIMATIE, n7442_2_pin4);
  not not_10 (BANI, n7442_2_pin5);
  not not_11 (REST, n7442_2_pin6);
  Multiplexer multiplexer_7 (.in0(1'b0), .in1(SWITCH[0]), .out(multiplexer_7_out), .sel(CLASA));
  Multiplexer multiplexer_8 (.in0(1'b0), .in1(SWITCH[0]), .out(multiplexer_8_out), .sel(LEGITIMATIE));
  and and_9 (and_9_out, multiplexer_7_out, OK);
  and and_10 (and_10_out, multiplexer_8_out, OK);
  J_K_Flip_Flop j_k_ff_1 (.J(and_9_out), .K(1'b0), .clk(CLK), .Q(j_k_ff_1_q), .reset(or_7_out));  // open: Qn, preset
  J_K_Flip_Flop j_k_ff_2 (.J(and_10_out), .K(1'b0), .clk(CLK), .Q(j_k_ff_2_q), .reset(or_8_out));  // open: Qn, preset
  Mem_Reg MEMORIE_PRET (.Clk(CLK), .Ld(1'b1), .Rst(RESET), .Data(multiplexer_10_out), .Q(SUMA_IN));
  Multiplexer #(.select(3), .width(8)) multiplexer_9 (
    .in0(SWITCH), .in1(SWITCH), .in2({8{1'b0}}), .in3({8{1'b0}}), .in4(SUMA_IN), .in5({8{1'b0}}), .in6(AR),
    .in7({8{1'b0}}), .out(multiplexer_9_out), .sel(MODE));
  or or_7 (or_7_out, start, RESET);
  or or_8 (or_8_out, start, RESET);
  CALCULARE_REST calculare_rest_1 (
    .EURO1(EURO1), .EURO2(EURO2), .EURO5(EURO5), .EURO10(EURO10), .EURO20(EURO20), .EURO50(EURO50),
    .VALOARE_REST(SUMA_OUT), .ENABLE(REST), .CLK(CLK), .REST_IMPOSIBIL(REST_IMP), .QEURO1(QEURO1),
    .QEURO2(QEURO2), .QEURO5(QEURO5), .QEURO10(QEURO10), .QEURO20(QEURO20), .QEURO50(QEURO50));
  Multiplexer #(.width(8)) multiplexer_10 (.in0(PRET), .in1(SUMA_OUT), .out(multiplexer_10_out), .sel(j_k_ff_3_q));
  insert_coin insert_coin_1 (
    .SUMA_INITIALA(SUMA_IN), .COIN_IN(SWITCH), .OK(OK), .ENABLE(BANI), .RST(start), .CLK(CLK), .REST(REST_t),
    .ZERO(insert_coin_1_zero), .SUMA_OUT(SUMA_OUT));
  decodificator decodificator_1 (.Bin_num(multiplexer_9_out), .Unitati(UNITATI), .Zeci(ZECI), .Sute(SUTE));
  J_K_Flip_Flop j_k_ff_3 (
    .J(insert_coin_1_zero), .K(1'b0), .clk(CLK), .Q(j_k_ff_3_q), .reset(or_9_out));  // open: Qn, preset
  or or_9 (or_9_out, start, RESET);
  Multiplexer #(.width(8)) multiplexer_11 (.in0(SUMA_OUT), .in1(PRET), .out(AR), .sel(REST_IMP));
  calculate_price calculate_price_1 (
    .KILOMETRI(MEMORIE_KM), .CLASA(j_k_ff_1_q), .LEGITIMATIE(j_k_ff_2_q), .CLK(CLK), .PRET(PRET));
  // also tied to GND on the sheet: n7442_2_pin12

  // Other names for the same wires on the sheet: B = BANI; C = CLASA; FINALE = FINAL; L = LEGITIMATIE; R = REST;
  //   BIT_0 = SWITCH[0]
endmodule

// VHDL entity UC, as the project stores it:
--------------------------------------------------------------------------------
-- Project :
-- File    :
-- Autor   :
-- Date    :
--
--------------------------------------------------------------------------------
-- Description :
--
--------------------------------------------------------------------------------

LIBRARY ieee;
USE ieee.std_logic_1164.all;

ENTITY UC IS
  PORT (START, OK, CLK, RESET: in std_logic;
  	   INSERT_MONEY: in std_logic;
  	   MODE: out std_logic_vector(2 downto 0);
  	   Waiting, FINALE :out std_logic;
  	   DEBUG : in std_logic
    );
END UC;

--------------------------------------------------------------------------------
--Complete your VHDL description below
--------------------------------------------------------------------------------

ARCHITECTURE TypeArchitecture OF UC IS

type Stare_T is (IDLE,MODE1,MODE2,MODE3,MODE4,MODE5, FIN);
Signal CURRENT_STATE , NEXT_STATE: Stare_T:= IDLE;
BEGIN
	

	process(CLK, RESET)
	begin
		If RESET='1' then CURRENT_STATE<=IDLE;
		else
			if rising_edge(CLK) then
				CURRENT_STATE <= NEXT_STATE;
			end if;
		end if;
	end process;
	

	process(CURRENT_STATE, START, OK)--stabilirea starii urmatoare
	begin
	Waiting<='0'; FINALE <= '0';
	if DEBUG = '0' then
		case CURRENT_STATE is
			when IDLE => Waiting <= '1'; MODE <= "000";
						if START='1' then NEXT_STATE <= MODE1;
						else NEXT_STATE <= IDLE;
						end if;
			when MODE1 => MODE <= "001";
					if OK='0' then NEXT_STATE <= MODE1;
					else NEXT_STATE <= MODE2;
					end if;
			when MODE2 => MODE <= "010";
					if OK='0' then NEXT_STATE <= MODE2;
					else NEXT_STATE <= MODE3;
					end if;
			when MODE3 => MODE <= "011";
					if OK='0' then NEXT_STATE<=MODE3;
					else NEXT_STATE<=MODE4;
					end if;
			when MODE4 => MODE <= "100";
					if OK='0' then NEXT_STATE<=MODE4;
					else 
						case INSERT_MONEY is
							when '1' => NEXT_STATE<=MODE5;
							when others => NEXT_STATE<=MODE4;
						end case;
					end if;
			when MODE5 => MODE <= "101";
					if OK='0' then NEXT_STATE<=MODE5;
					else NEXT_STATE<= FIN;
					end if;
			when FIN => FINALE <= '1'; MODE <= "110";
					if Start='0' then NEXT_STATE<=FIN;
					else NEXT_STATE<= IDLE;
					end if;
			end case;
		end if;
		end process;		
					

END TypeArchitecture;

// VHDL entity Binary_to_decimal_converter, as the project stores it:
--------------------------------------------------------------------------------
-- Project :
-- File    :
-- Autor   :
-- Date    :
--
--------------------------------------------------------------------------------
-- Description :
--
--------------------------------------------------------------------------------

LIBRARY ieee;
USE ieee.std_logic_1164.all;
USE ieee.std_logic_unsigned.all;
USE ieee.std_logic_arith.all;

ENTITY Binary_to_decimal_converter IS
  PORT (
 Bin_num: in std_logic_vector(7 downto 0);
  		Unit: out std_logic_vector(3 downto 0);
  		Decimal: out std_logic_vector(3 downto 0);
  		Hundred: out std_logic_vector(3 downto 0) 
    );
END Binary_to_decimal_converter;

--------------------------------------------------------------------------------
--Complete your VHDL description below
--------------------------------------------------------------------------------

ARCHITECTURE comport OF Binary_to_decimal_converter IS

signal num_int, zeci_int: integer:=0;
signal u,z,s: integer:=0;
BEGIN

	num_int<=conv_integer(bin_num);
	s <= num_int / 100;
	zeci_int <= num_int rem 100;
	z <= zeci_int /10;
	u <= zeci_int rem 10;
	
	process(u)
	begin
		case u is
		when 0 => unit <= x"0";
		when 1 => unit <= x"1";
		when 2 => unit <= x"2";
		when 3 => unit <= x"3";
		when 4 => unit <= x"4";
		when 5 => unit <= x"5";
		when 6 => unit <= x"6";
		when 7 => unit <= x"7";
		when 8 => unit <= x"8";
		when 9 => unit <= x"9";
		when others => unit <=x"f";
		end case;
	end process;
	process(z)
	begin
		case z is
		when 0 => Decimal <= x"0";
		when 1 => Decimal <= x"1";
		when 2 => Decimal <= x"2";
		when 3 => Decimal <= x"3";
		when 4 => Decimal <= x"4";
		when 5 => Decimal <= x"5";
		when 6 => Decimal <= x"6";
		when 7 => Decimal <= x"7";
		when 8 => Decimal <= x"8";
		when 9 => Decimal <= x"9";
		when others => Decimal <=x"f";
		end case;
	end process;
	
	process(s)
	begin
		case s is
		when 0 => Hundred <= x"0";
		when 1 => Hundred <= x"1";
		when 2 => Hundred <= x"2";
		when 3 => Hundred <= x"3";
		when 4 => Hundred <= x"4";
		when 5 => Hundred <= x"5";
		when 6 => Hundred <= x"6";
		when 7 => Hundred <= x"7";
		when 8 => Hundred <= x"8";
		when 9 => Hundred <= x"9";
		when others => Hundred <=x"f";
		end case;
	end process;
		 

	
END comport;

// VHDL entity Mem_Reg, as the project stores it:
--------------------------------------------------------------------------------
-- Project :
-- File    :
-- Autor   :
-- Date    :
--
--------------------------------------------------------------------------------
-- Description :
-- 
--------------------------------------------------------------------------------

LIBRARY ieee;
USE ieee.std_logic_1164.all;

ENTITY Mem_Reg IS
  PORT (
 Clk,Ld,Rst: in std_logic;
  		Data: in std_logic_vector(7 downto 0);
  		Q:out std_logic_vector(7 downto 0) 
    );
END Mem_Reg;

--------------------------------------------------------------------------------
--Complete your VHDL description below
--------------------------------------------------------------------------------

ARCHITECTURE TypeArchitecture OF Mem_Reg IS

BEGIN

	process(clk)
	variable reg: std_logic_vector(7 downto 0):=(others=>'0');
	begin
		if rising_edge(clk) then
			if Rst='1' then reg:=(others=>'0');
			else if Ld='0' then reg:=reg;
				else reg:=Data;
				end if;
			end if;
		end if;
	Q<=reg;
	end process;

END TypeArchitecture;

// VHDL entity calculate_price, as the project stores it:
LIBRARY ieee;
USE ieee.std_logic_1164.all;
USE ieee.std_logic_unsigned.all;
use ieee.numeric_std.all;

entity calculate_price is
    Port ( 
        KILOMETRI : in  std_logic_vector(7 downto 0);
        CLASA : in  std_logic;
        LEGITIMATIE : in std_logic;
        CLK : in std_logic;
        PRET : out std_logic_vector(7 downto 0)
    );
end calculate_price;

architecture Behavioral of calculate_price is
    signal float_kilometri : integer := 0;
    signal price : integer:= 0;
    signal aux : integer := 0;
begin
	
	float_kilometri <= conv_integer(KILOMETRI);
	process(CLK)
	begin
		case CLASA is
			when '0' => price <= float_kilometri - float_kilometri / 4; --25% reducere
			when others => price <= float_kilometri;
		end case;
		case LEGITIMATIE is
			when '1' => aux <=  price / 2; --50% reducere
			when others => aux <= price;
		end case;
		PRET <= std_logic_vector(to_unsigned(aux, 8));
	end process;
	
	
	
end Behavioral;

// VHDL entity insert_coin, as the project stores it:
LIBRARY ieee;
USE ieee.std_logic_1164.all;
USE ieee.std_logic_unsigned.all;
use ieee.numeric_std.all;

entity insert_coin is
    Port ( 
        SUMA_INITIALA : in  std_logic_vector(7 downto 0);
        COIN_IN : in  std_logic_vector(7 downto 0);
        OK : in std_logic;
        ENABLE : in std_logic;
        REST : inout std_logic;
        RST : in std_logic;
        CLK : in std_logic;
        ZERO : out std_logic;
        SUMA_OUT : inout std_logic_vector(7 downto 0)
    );
end insert_coin;

architecture Behavioral of insert_coin is
    signal SUMA_INT : integer := 0;
    signal REZULT : integer := 0;

begin
	
	SUMA_INT <= conv_integer(SUMA_INITIALA);
	--process(CLK)
	--begin
		--if RST = '1' then
		--ZERO <= '0';
		--REST <= '0';
		--end if;
	--end process;
	process(CLK)
	begin
	if RST = '1' then
		ZERO <= '0';
		REST <= '0';
	elsif ENABLE = '1' then
		if OK = '1' and REST = '0' then
		case COIN_IN is
			when "00000001" => REZULT <= SUMA_INT - 1; ZERO <= '1'; --1 euro
			when "00000010" => REZULT <= SUMA_INT - 2; ZERO <= '1';--2 euro
			when "00000100" => REZULT <= SUMA_INT - 5; ZERO <= '1';--5 euro
			when "00001000" => REZULT <= SUMA_INT - 10; ZERO <= '1';--10 euro
			when "00010000" => REZULT <= SUMA_INT - 20; ZERO <= '1';--20 euro
			when "00100000" => REZULT <= SUMA_INT - 50; ZERO <= '1';--50 euro
			when others => REZULT <= SUMA_INT;
		end case;
		if REZULT < 0 then
			REST <= '1';
			REZULT <= -REZULT;
		end if;
		SUMA_OUT <= std_logic_vector(to_unsigned(REZULT, 8));
		end if;
	end if;
	end process;
	
	
end Behavioral;

// VHDL entity CALCULARE_REST, as the project stores it:
LIBRARY ieee;
USE ieee.std_logic_1164.all;
USE ieee.std_logic_unsigned.all;
use ieee.numeric_std.all;

ENTITY CALCULARE_REST IS
  PORT (
  	EURO1 : in std_logic_vector(7 downto 0);
  	EURO2 : in std_logic_vector(7 downto 0);
  	EURO5 : in std_logic_vector(7 downto 0);
  	EURO10 : in std_logic_vector(7 downto 0);
  	EURO20 : in std_logic_vector(7 downto 0);
  	EURO50 : in std_logic_vector(7 downto 0);
  	VALOARE_REST : in std_logic_vector(7 downto 0);
  	ENABLE : in std_logic;
  	CLK : in std_logic;
  	REST_IMPOSIBIL : out std_logic;
  	QEURO1 : out std_logic_vector(7 downto 0);
  	QEURO2 : out std_logic_vector(7 downto 0);
  	QEURO5 : out std_logic_vector(7 downto 0);
  	QEURO10 : out std_logic_vector(7 downto 0);
  	QEURO20 : out std_logic_vector(7 downto 0);
  	QEURO50 : out std_logic_vector(7 downto 0)
  	
    );
END CALCULARE_REST;


ARCHITECTURE TypeArchitecture OF CALCULARE_REST IS

	signal VALOARE_REST_INT : integer:= conv_integer(VALOARE_REST);
	signal NR_E1 : integer := conv_integer(EURO1);
	signal NR_E2 : integer := conv_integer(EURO2);
	signal NR_E5 : integer := conv_integer(EURO5);
	signal NR_E10 : integer := conv_integer(EURO10);
	signal NR_E20 : integer := conv_integer(EURO20);
	signal NR_E50 : integer := conv_integer(EURO50);
	
BEGIN

	process(clk) is
		variable x : integer := VALOARE_REST_INT;
		variable ok : integer := 0;
		variable e1 : integer;
		variable e2 : integer;
		variable e5 : integer;
		variable e10 : integer;
		variable e20 : integer;
		variable e50 : integer;
		
	begin
	if ENABLE = '1' then
		NR_E1 <= conv_integer(EURO1);
		NR_E2 <= conv_integer(EURO2);
		NR_E5 <= conv_integer(EURO5);
		NR_E10 <= conv_integer(EURO10);
		NR_E20 <= conv_integer(EURO20);
		NR_E50 <= conv_integer(EURO50);
		VALOARE_REST_INT <= conv_integer(VALOARE_REST);
		x:= VALOARE_REST_INT;
		e1 := NR_E1;
		e2 := NR_E2;
		e5 := NR_E5;
		e10 := NR_E10;
		e20 := NR_E20;
		e50 := NR_E50;
		ok := 1;
		while x > 0 and ok = 1 loop
			if x >= 50 and e50 > 0 then
				x := x - 50;
				e50 := e50 - 1;
			elsif x >= 20 and e20 > 0 then
				x := x - 20;
				e20 := e20 - 1;
			elsif x >= 10 and e10 > 0 then
				x := x - 10;
				e10 := e10 - 1;
			elsif x >= 5 and e5 > 0 then
				x := x - 5;
				e5 := e5 - 1;
			elsif x >= 2 and e2 > 0 then
				x := x - 2;
				e2 := e2 - 1;
			elsif x >= 1 and e1 > 0 then
				x := x - 1;
				e1 := e1 - 1;
			else ok := 0;
			end if;
		end loop;
		if ok = 0 then
			REST_IMPOSIBIL <= '1';
			QEURO1 <= EURO1;
			QEURO2 <= EURO2;
			QEURO5 <= EURO5;
			QEURO10 <= EURO10;
			QEURO20 <= EURO20;
			QEURO50 <= EURO50;
		else
			REST_IMPOSIBIL <= '0';
			
			QEURO1 <= std_logic_vector(to_unsigned(e1, 8));
			QEURO2 <= std_logic_vector(to_unsigned(e2, 8));
			QEURO5 <= std_logic_vector(to_unsigned(e5, 8));
			QEURO10 <= std_logic_vector(to_unsigned(e10, 8));
			QEURO20 <= std_logic_vector(to_unsigned(e20, 8));
			QEURO50 <= std_logic_vector(to_unsigned(e50, 8));
		end if;
		ok := 1;
	end if;
	end process;

END TypeArchitecture;
